// Logisim project project.circ as structural Verilog: 4 circuits, main circuit main
module main (
  input  PCclr,
  input  RegClr,
  input  RAMclr
);

  wire and_1_out, Clock_out, control_unit_1_alusrc, control_unit_1_binv, control_unit_1_branch,
       control_unit_1_cin, control_unit_1_jump, control_unit_1_ld, control_unit_1_memen,
       control_unit_1_memtoreg, control_unit_1_regdst, control_unit_1_str, control_unit_1_wc,
       n18_bit_alu_1_zero;
  wire [1:0] control_unit_1_aluop;
  wire [3:0] multiplexer_1_out;
  wire [11:0] rom_1_data;
  wire [17:0] adder_1_out, bit_extender_1_out, bit_extender_2_out, multiplexer_2_out, multiplexer_3_out,
       multiplexer_4_out, multiplexer_5_out, n18_bit_alu_1_f, ram_1_data, register_1_q,
       register_file_1_read_data_1, register_file_1_read_data_2;
  wire [17:12] rom_1_data_2;

  Button Clock (.out(Clock_out));
  Register #(.width(18)) register_1 (
    .D(multiplexer_4_out), .Q(register_1_q), .clk(Clock_out), .clr(PCclr));  // open: en
  Adder #(.width(18)) adder_1 (.a(18'h1), .b(register_1_q), .out(adder_1_out));  // open: cin, cout
  ROM #(.addrWidth(18), .dataWidth(18)) rom_1 (.addr(register_1_q), .data({rom_1_data_2, rom_1_data}));  // open: sel
  assign bit_extender_1_out = {{6{1'b0}}, rom_1_data};  // Bit_Extender bit_extender_1
  Multiplexer #(.width(4)) multiplexer_1 (
    .in0(rom_1_data[3:0]), .in1(rom_1_data[7:4]), .out(multiplexer_1_out), .sel(control_unit_1_regdst));  // open: en
  assign bit_extender_2_out = {{14{1'b0}}, rom_1_data[3:0]};  // Bit_Extender bit_extender_2
  Control_Unit control_unit_1 (
    .Opcode(rom_1_data_2), .Binv(control_unit_1_binv), .Cin(control_unit_1_cin), .WC(control_unit_1_wc),
    .MemToReg(control_unit_1_memtoreg), .ALUsrc(control_unit_1_alusrc), .RegDst(control_unit_1_regdst),
    .Str(control_unit_1_str), .Ld(control_unit_1_ld), .Branch(control_unit_1_branch),
    .MEMen(control_unit_1_memen), .Jump(control_unit_1_jump), .ALUop(control_unit_1_aluop));
  REGISTER_file register_file_1 (
    .Write_register(multiplexer_1_out), .rs(rom_1_data[11:8]), .rt(rom_1_data[7:4]), .wc(control_unit_1_wc),
    .clk(Clock_out), .Write_data(multiplexer_5_out), .clear(RegClr),
    .read_data_1(register_file_1_read_data_1), .read_data_2(register_file_1_read_data_2));
  Multiplexer #(.width(18)) multiplexer_2 (
    .in0(register_file_1_read_data_2), .in1(bit_extender_2_out), .out(multiplexer_2_out),
    .sel(control_unit_1_alusrc));  // open: en
  _18_Bit_ALU u_18_bit_alu_1 (
    .ALUop(control_unit_1_aluop), .Binv(control_unit_1_binv), .F(n18_bit_alu_1_f),
    .A(register_file_1_read_data_1), .B(multiplexer_2_out), .Cin(control_unit_1_cin),
    .Zero(n18_bit_alu_1_zero));  // open: Cout
  and and_1 (and_1_out, n18_bit_alu_1_zero, control_unit_1_branch);
  Multiplexer #(.width(18)) multiplexer_3 (
    .in0(adder_1_out), .in1(bit_extender_2_out), .out(multiplexer_3_out), .sel(and_1_out));  // open: en
  RAM #(.addrWidth(18), .dataWidth(18), .bus("separate")) ram_1 (
    .addr(n18_bit_alu_1_f), .din(register_file_1_read_data_2), .data(ram_1_data), .str(control_unit_1_str),
    .sel(control_unit_1_memen), .clk(Clock_out), .ld(control_unit_1_ld), .clr(RAMclr));
  Multiplexer #(.width(18)) multiplexer_4 (
    .in0(multiplexer_3_out), .in1(bit_extender_1_out), .out(multiplexer_4_out), .sel(control_unit_1_jump));  // open: en
  Multiplexer #(.width(18)) multiplexer_5 (
    .in0(n18_bit_alu_1_f), .in1(ram_1_data), .out(multiplexer_5_out), .sel(control_unit_1_memtoreg));  // open: en

  // Notes on the sheet:
  //   contents of rom_1 (hex, n*v repeats v):
  //   9013 4020 4033 329 4042 a141 4112 4221 8003 3040
endmodule

module _18_Bit_ALU (
  input  [17:0] A,
  input  [17:0] B,
  input  [1:0] ALUop,
  input  Cin,
  input  Binv,
  output [17:0] F,
  output Zero,
  output Cout
);

  wire comparator_1_lt;
  wire [4:0] bit_extender_1_out;
  wire [17:0] adder_1_out, and_1_out, bit_extender_2_out, multiplexer_1_out, not_1_out, shifter_1_out;

  Bit_Extender #(.in_width(18), .out_width(5)) bit_extender_1 (.in(B), .out(bit_extender_1_out));
  Comparator #(.width(18)) comparator_1 (.a(A), .b(B), .eq(Zero), .lt(comparator_1_lt));  // open: gt
  Multiplexer #(.width(18), .enable("false")) multiplexer_1 (
    .in0(B), .in1(not_1_out), .out(multiplexer_1_out), .sel(Binv));
  assign not_1_out = ~B;  // NOT_Gate not_1, 18 bits wide
  Shifter #(.width(18)) shifter_1 (.in(A), .\dist (bit_extender_1_out), .out(shifter_1_out));
  assign and_1_out = A & B;  // AND_Gate and_1, 18 bits wide
  assign bit_extender_2_out = {{17{1'b0}}, comparator_1_lt};  // Bit_Extender bit_extender_2
  Adder #(.width(18)) adder_1 (.a(A), .b(multiplexer_1_out), .out(adder_1_out), .cin(Cin), .cout(Cout));
  Multiplexer #(.select(2), .width(18)) multiplexer_2 (
    .in0(shifter_1_out), .in1(and_1_out), .in2(bit_extender_2_out), .in3(adder_1_out), .out(F), .sel(ALUop));  // open: en
endmodule

module REGISTER_file (
  input  [3:0] Write_register,
  input  [3:0] rs,
  input  [3:0] rt,
  input  wc,
  input  clk,
  input  clear,
  input  [17:0] Write_data,
  output [17:0] read_data_1,
  output [17:0] read_data_2
);

  wire and_1_out, and_2_out, and_3_out, and_4_out, and_5_out, and_6_out, and_7_out, and_8_out, and_9_out,
       and_10_out, and_11_out, and_12_out, and_13_out, and_14_out, and_15_out, and_16_out, decoder_1_out0,
       decoder_1_out1, decoder_1_out2, decoder_1_out3, decoder_1_out4, decoder_1_out5, decoder_1_out6,
       decoder_1_out7, decoder_1_out8, decoder_1_out9, decoder_1_out10, decoder_1_out11, decoder_1_out12,
       decoder_1_out13, decoder_1_out14, decoder_1_out15;
  wire [17:0] register_1_q, register_2_q, register_3_q, register_4_q, register_5_q, register_6_q,
       register_7_q, register_8_q, register_9_q, register_10_q, register_11_q, register_12_q, register_13_q,
       register_14_q, register_15_q, register_16_q;

  Decoder #(.select(4)) decoder_1 (
    .out0(decoder_1_out0), .out1(decoder_1_out1), .out2(decoder_1_out2), .out3(decoder_1_out3),
    .out4(decoder_1_out4), .out5(decoder_1_out5), .out6(decoder_1_out6), .out7(decoder_1_out7),
    .out8(decoder_1_out8), .out9(decoder_1_out9), .out10(decoder_1_out10), .out11(decoder_1_out11),
    .out12(decoder_1_out12), .out13(decoder_1_out13), .out14(decoder_1_out14), .out15(decoder_1_out15),
    .sel(Write_register));  // open: en
  and and_1 (and_1_out, decoder_1_out0, wc);
  and and_2 (and_2_out, decoder_1_out1, wc);
  and and_3 (and_3_out, decoder_1_out2, wc);
  and and_4 (and_4_out, decoder_1_out3, wc);
  and and_5 (and_5_out, decoder_1_out4, wc);
  and and_6 (and_6_out, decoder_1_out5, wc);
  and and_7 (and_7_out, decoder_1_out6, wc);
  and and_8 (and_8_out, decoder_1_out7, wc);
  and and_9 (and_9_out, decoder_1_out8, wc);
  and and_10 (and_10_out, decoder_1_out9, wc);
  and and_11 (and_11_out, decoder_1_out10, wc);
  and and_12 (and_12_out, decoder_1_out11, wc);
  and and_13 (and_13_out, decoder_1_out12, wc);
  and and_14 (and_14_out, decoder_1_out13, wc);
  and and_15 (and_15_out, decoder_1_out14, wc);
  and and_16 (and_16_out, decoder_1_out15, wc);
  Register #(.width(18)) register_1 (.D(Write_data), .en(and_1_out), .Q(register_1_q), .clk(clk), .clr(clear));
  Register #(.width(18)) register_2 (.D(Write_data), .en(and_2_out), .Q(register_2_q), .clk(clk), .clr(clear));
  Register #(.width(18)) register_3 (.D(Write_data), .en(and_3_out), .Q(register_3_q), .clk(clk), .clr(clear));
  Register #(.width(18)) register_4 (.D(Write_data), .en(and_4_out), .Q(register_4_q), .clk(clk), .clr(clear));
  Register #(.width(18)) register_5 (.D(Write_data), .en(and_5_out), .Q(register_5_q), .clk(clk), .clr(clear));
  Register #(.width(18)) register_6 (.D(Write_data), .en(and_6_out), .Q(register_6_q), .clk(clk), .clr(clear));
  Register #(.width(18)) register_7 (.D(Write_data), .en(and_7_out), .Q(register_7_q), .clk(clk), .clr(clear));
  Register #(.width(18)) register_8 (.D(Write_data), .en(and_8_out), .Q(register_8_q), .clk(clk), .clr(clear));
  Register #(.width(18)) register_9 (.D(Write_data), .en(and_9_out), .Q(register_9_q), .clk(clk), .clr(clear));
  Register #(.width(18)) register_10 (.D(Write_data), .en(and_10_out), .Q(register_10_q), .clk(clk), .clr(clear));
  Register #(.width(18)) register_11 (.D(Write_data), .en(and_11_out), .Q(register_11_q), .clk(clk), .clr(clear));
  Register #(.width(18)) register_12 (.D(Write_data), .en(and_12_out), .Q(register_12_q), .clk(clk), .clr(clear));
  Register #(.width(18)) register_13 (.D(Write_data), .en(and_13_out), .Q(register_13_q), .clk(clk), .clr(clear));
  Register #(.width(18)) register_14 (.D(Write_data), .en(and_14_out), .Q(register_14_q), .clk(clk), .clr(clear));
  Register #(.width(18)) register_15 (.D(Write_data), .en(and_15_out), .Q(register_15_q), .clk(clk), .clr(clear));
  Register #(.width(18)) register_16 (.D(Write_data), .en(and_16_out), .Q(register_16_q), .clk(clk), .clr(clear));
  Multiplexer #(.select(4), .width(18)) multiplexer_1 (
    .in0(register_1_q), .in1(register_2_q), .in2(register_3_q), .in3(register_4_q), .in4(register_5_q),
    .in5(register_6_q), .in6(register_7_q), .in7(register_8_q), .in8(register_9_q), .in9(register_10_q),
    .in10(register_11_q), .in11(register_12_q), .in12(register_13_q), .in13(register_14_q),
    .in14(register_15_q), .in15(register_16_q), .out(read_data_1), .sel(rs));  // open: en
  Multiplexer #(.select(4), .width(18)) multiplexer_2 (
    .in0(register_1_q), .in1(register_2_q), .in2(register_3_q), .in3(register_4_q), .in4(register_5_q),
    .in5(register_6_q), .in6(register_7_q), .in7(register_8_q), .in8(register_9_q), .in9(register_10_q),
    .in10(register_11_q), .in11(register_12_q), .in12(register_13_q), .in13(register_14_q),
    .in14(register_15_q), .in15(register_16_q), .out(read_data_2), .sel(rt));  // open: en
endmodule

module Control_Unit (
  input  [5:0] Opcode,
  output [1:0] ALUop,
  output Binv,
  output Cin,
  output WC,
  output MemToReg,
  output ALUsrc,
  output RegDst,
  output Str,
  output Ld,
  output Branch,
  output MEMen,
  output Jump
);

  wire decoder_1_out1, decoder_1_out2, decoder_1_out4, decoder_1_out5, decoder_1_out7, decoder_1_out10;
  wire [3:0] bit_extender_1_out;

  Bit_Extender #(.in_width(6), .out_width(4)) bit_extender_1 (.in(Opcode), .out(bit_extender_1_out));
  Decoder #(.select(4)) decoder_1 (
    .out0(Branch), .out1(decoder_1_out1), .out2(decoder_1_out2), .out3(Str), .out4(decoder_1_out4),
    .out5(decoder_1_out5), .out6(Binv), .out7(decoder_1_out7), .out8(Jump), .out9(Ld),
    .out10(decoder_1_out10), .sel(bit_extender_1_out));  // open: out11, out12, out13, out14, out15, en
  or or_1 (ALUop[0], decoder_1_out1, decoder_1_out2, Str, decoder_1_out4, Binv, Ld);
  or or_2 (ALUop[1], decoder_1_out1, Str, decoder_1_out4, Binv, decoder_1_out7, Ld);
  or or_3 (WC, decoder_1_out1, decoder_1_out2, decoder_1_out4, Binv, decoder_1_out7, Ld, decoder_1_out10);
  or or_4 (ALUsrc, Str, decoder_1_out4, Ld);
  or or_5 (RegDst, decoder_1_out4, Ld);
  or or_6 (MEMen, Str, Ld);

  assign Cin = Binv;
  assign MemToReg = Ld;
endmodule
